// Logisim project First.circ as structural Verilog
module ALU (
  input  [31:0] A,
  input  [31:0] B,
  input  [3:0] in_3,
  output [31:0] out_4
);

  wire comparator_1_lt, comparator_2_lt;
  wire [31:0] adder_1_out, and_1_out, bit_extender_1_out, bit_extender_2_out, or_1_out, shifter_1_out,
       shifter_2_out, shifter_3_out, subtractor_1_out, xor_1_out;

  assign and_1_out = A & B;  // AND_Gate and_1, 32 bits wide
  assign or_1_out = A | B;  // OR_Gate or_1, 32 bits wide
  Adder #(.width(32)) adder_1 (.a(A), .b(B), .out(adder_1_out));  // open: cin, cout
  Subtractor #(.width(32)) subtractor_1 (.a(A), .b(B), .out(subtractor_1_out));  // open: bin, bout
  Shifter #(.width(32)) shifter_1 (.in(A), .\dist (B[4:0]), .out(shifter_1_out));
  Shifter #(.shift("lr"), .width(32)) shifter_2 (.in(A), .\dist (B[4:0]), .out(shifter_2_out));
  Shifter #(.shift("ar"), .width(32)) shifter_3 (.in(A), .\dist (B[4:0]), .out(shifter_3_out));
  Comparator #(.width(32)) comparator_1 (.a(A), .b(B), .lt(comparator_1_lt));  // open: gt, eq
  Comparator #(.mode("unsigned"), .width(32)) comparator_2 (.a(A), .b(B), .lt(comparator_2_lt));  // open: gt, eq
  assign xor_1_out = A ^ B;  // XOR_Gate xor_1, 32 bits wide
  assign bit_extender_1_out = {{31{1'b0}}, comparator_1_lt};  // Bit_Extender bit_extender_1
  assign bit_extender_2_out = {{31{1'b0}}, comparator_2_lt};  // Bit_Extender bit_extender_2
  Multiplexer #(.select(4), .width(32)) multiplexer_1 (
    .in0(and_1_out), .in1(or_1_out), .in2(adder_1_out), .in3(subtractor_1_out), .in4(xor_1_out),
    .in5(shifter_1_out), .in6(shifter_2_out), .in7(shifter_3_out), .in8(bit_extender_1_out),
    .in9(bit_extender_2_out), .in10(B), .out(out_4), .sel(in_3));  // open: in11, in12, in13, in14, in15
endmodule

module Registers (
  input  [31:0] in_1,
  input  clk,
  input  WrEn,
  input  [1:0] WrIdx,
  input  [31:0] WrData,
  input  [1:0] R1Idx,
  input  [1:0] R2Idx,
  output [31:0] Reg1,
  output [31:0] Reg2
);

  wire decoder_1_out1, decoder_1_out2, decoder_1_out3;
  wire [31:0] x1_q, x2_q, x3_q;

  Decoder #(.select(2)) decoder_1 (
    .out1(decoder_1_out1), .out2(decoder_1_out2), .out3(decoder_1_out3), .sel(WrIdx), .en(WrEn));  // open: out0
  Register #(.width(32)) x1 (.D(WrData), .en(decoder_1_out1), .clk(clk), .Q(x1_q));  // open: clr
  Register #(.width(32)) x2 (.D(WrData), .en(decoder_1_out2), .clk(clk), .Q(x2_q));  // open: clr
  Register #(.width(32)) x3 (.D(WrData), .en(decoder_1_out3), .clk(clk), .Q(x3_q));  // open: clr
  Multiplexer #(.select(2), .width(32)) multiplexer_1 (
    .in0(in_1), .in1(x1_q), .in2(x2_q), .in3(x3_q), .out(Reg1), .sel(R1Idx));
  Multiplexer #(.select(2), .width(32)) multiplexer_2 (
    .in0(in_1), .in1(x1_q), .in2(x2_q), .in3(x3_q), .out(Reg2), .sel(R2Idx));
endmodule

module Bank8 (
  input  clk,
  input  WrEn,
  input  [2:0] WrIdx,
  input  [2:0] R1Idx,
  input  [31:0] WrData,
  input  [2:0] R2Idx,
  output [31:0] Reg1,
  output [31:0] Reg2
);

  wire decoder_1_out0, decoder_1_out1, decoder_1_out2, decoder_1_out3, decoder_1_out4, decoder_1_out5,
       decoder_1_out6, decoder_1_out7;
  wire [31:0] x0_q, x1_q, x2_q, x3_q, x4_q, x5_q, x6_q, x7_q;

  Decoder #(.select(3)) decoder_1 (
    .out0(decoder_1_out0), .out1(decoder_1_out1), .out2(decoder_1_out2), .out3(decoder_1_out3),
    .out4(decoder_1_out4), .out5(decoder_1_out5), .out6(decoder_1_out6), .out7(decoder_1_out7), .sel(WrIdx),
    .en(WrEn));
  Register #(.width(32)) x0 (.D(WrData), .en(decoder_1_out0), .clk(clk), .Q(x0_q));  // open: clr
  Register #(.width(32)) x1 (.D(WrData), .en(decoder_1_out1), .clk(clk), .Q(x1_q));  // open: clr
  Register #(.width(32)) x2 (.D(WrData), .en(decoder_1_out2), .clk(clk), .Q(x2_q));  // open: clr
  Register #(.width(32)) x3 (.D(WrData), .en(decoder_1_out3), .clk(clk), .Q(x3_q));  // open: clr
  Register #(.width(32)) x4 (.D(WrData), .en(decoder_1_out4), .clk(clk), .Q(x4_q));  // open: clr
  Register #(.width(32)) x5 (.D(WrData), .en(decoder_1_out5), .clk(clk), .Q(x5_q));  // open: clr
  Register #(.width(32)) x6 (.D(WrData), .en(decoder_1_out6), .clk(clk), .Q(x6_q));  // open: clr
  Register #(.width(32)) x7 (.D(WrData), .en(decoder_1_out7), .clk(clk), .Q(x7_q));  // open: clr
  Multiplexer #(.select(3), .width(32)) multiplexer_1 (
    .in0(x0_q), .in1(x1_q), .in2(x2_q), .in3(x3_q), .in4(x4_q), .in5(x5_q), .in6(x6_q), .in7(x7_q),
    .out(Reg1), .sel(R1Idx));
  Multiplexer #(.select(3), .width(32)) multiplexer_2 (
    .in0(x0_q), .in1(x1_q), .in2(x2_q), .in3(x3_q), .in4(x4_q), .in5(x5_q), .in6(x6_q), .in7(x7_q),
    .out(Reg2), .sel(R2Idx));
endmodule

module RegFile (
  input  clk,
  input  WrEn,
  input  [4:0] WrIdx,
  input  [31:0] WrData,
  input  [4:0] R1Idx,
  input  [4:0] R2Idx,
  input  [4:0] in_7,
  output [31:0] out_8,
  output [31:0] Reg2
);

  wire and_1_out, comparator_1_eq, decoder_1_out0, not_1_out;
  wire [31:0] bank8_1_reg1, bank8_1_reg2, bank8_2_reg1, bank8_2_reg2, bank8_3_reg1, bank8_3_reg2,
       bank8_4_reg1, bank8_4_reg2;

  not not_1 (not_1_out, comparator_1_eq);
  Comparator #(.width(5)) comparator_1 (.a(WrIdx), .b(in_7), .eq(comparator_1_eq));  // open: gt, lt
  and and_1 (and_1_out, WrEn, not_1_out);
  Decoder #(.select(2)) decoder_1 (.out0(decoder_1_out0), .sel(WrIdx[4:3]), .en(and_1_out));  // open: out1, out2, out3
  Bank8 bank8_1 (
    .clk(clk), .WrEn(decoder_1_out0), .WrIdx(WrIdx[2:0]), .R1Idx(R1Idx[2:0]), .WrData(WrData),
    .R2Idx(R2Idx[2:0]), .Reg1(bank8_1_reg1), .Reg2(bank8_1_reg2));
  Bank8 bank8_2 (
    .clk(clk), .WrEn(decoder_1_out0), .WrIdx(WrIdx[2:0]), .R1Idx(R1Idx[2:0]), .WrData(WrData),
    .R2Idx(R2Idx[2:0]), .Reg1(bank8_2_reg1), .Reg2(bank8_2_reg2));
  Bank8 bank8_3 (
    .clk(clk), .WrEn(decoder_1_out0), .WrIdx(WrIdx[2:0]), .R1Idx(R1Idx[2:0]), .WrData(WrData),
    .R2Idx(R2Idx[2:0]), .Reg1(bank8_3_reg1), .Reg2(bank8_3_reg2));
  Bank8 bank8_4 (
    .clk(clk), .WrEn(decoder_1_out0), .WrIdx(WrIdx[2:0]), .R1Idx(R1Idx[2:0]), .WrData(WrData),
    .R2Idx(R2Idx[2:0]), .Reg1(bank8_4_reg1), .Reg2(bank8_4_reg2));
  Multiplexer #(.select(2), .width(32)) multiplexer_1 (
    .in0(bank8_1_reg1), .in1(bank8_2_reg1), .in2(bank8_3_reg1), .in3(bank8_4_reg1), .out(out_8),
    .sel(R1Idx[4:3]));
  Multiplexer #(.select(2), .width(32)) multiplexer_2 (
    .in0(bank8_1_reg2), .in1(bank8_2_reg2), .in2(bank8_3_reg2), .in3(bank8_4_reg2), .out(Reg2),
    .sel(R2Idx[4:3]));

  // Notes on the sheet:
  //   Reg1
endmodule

module ImmGen (
  input  [31:0] instr,
  input  [31:0] in_2,
  input  [2:0] ImmSel,
  input  in_4,
  input  [11:0] in_5,
  output [31:0] imm
);

  wire [31:0] bit_extender_1_out, bit_extender_2_out, bit_extender_3_out, bit_extender_4_out;

  assign bit_extender_1_out = {{20{instr[31]}}, instr[31:20]};  // Bit_Extender bit_extender_1
  assign bit_extender_2_out = {{20{instr[31]}}, {instr[31:25], instr[11:7]}};  // Bit_Extender bit_extender_2
  assign bit_extender_3_out = {{19{instr[31]}}, {instr[31], instr[7], instr[30:25], instr[11:8], in_4}};  // Bit_Extender bit_extender_3
  assign bit_extender_4_out = {{11{instr[31]}}, {instr[31], instr[19:12], instr[20], instr[30:21], in_4}};  // Bit_Extender bit_extender_4
  Multiplexer #(.select(3), .width(32)) multiplexer_1 (
    .in0(bit_extender_1_out), .in1(bit_extender_2_out), .in2(bit_extender_3_out), .in3({instr[31:12], in_5}),
    .in4(bit_extender_4_out), .in5(in_2), .in6(in_2), .in7(in_2), .out(imm), .sel(ImmSel));
endmodule

module InstrMem (
  input  [31:0] addr,
  output [31:0] instr
);

  ROM #(.addrWidth(10), .dataWidth(32)) rom_1 (.addr(addr[11:2]), .data(instr));

  // Notes on the sheet:
  //   contents of rom_1 (hex, n*v repeats v):
  //   500093 700113 2081b3 302023 10217
endmodule

module DataMem (
  input  [31:0] addr,
  input  WrEn,
  input  in_3,
  input  clk,
  input  [31:0] din,
  output [31:0] dout
);

  RAM #(.addrWidth(10), .dataWidth(32)) ram_1 (
    .addr(addr[11:2]), .we(WrEn), .oe(in_3), .clk(clk), .din(din), .dout(dout));
endmodule

module MainDecoder (
  input  [31:0] instr,
  output [1:0] ALUOp,
  output Jump,
  output Branch,
  output [1:0] WBSel,
  output MemWrite,
  output [12:0] ctrl,
  output ALUSrcB,
  output ALUSrcA,
  output RegWrite,
  output [2:0] ImmSel
);

  ROM #(.addrWidth(7), .dataWidth(13)) rom_1 (
    .addr(instr[6:0]), .data({ctrl[12:9], ALUSrcA, ALUSrcB, ctrl[6:4], Branch, ctrl[2], ALUOp}));

  assign {ctrl[8:7], ctrl[3], ctrl[1:0]} = {ALUSrcA, ALUSrcB, Branch, ALUOp};
  assign ImmSel = ctrl[12:10];
  assign Jump = ctrl[2];
  assign MemWrite = ctrl[6];
  assign RegWrite = ctrl[9];
  assign WBSel = ctrl[5:4];

  // Notes on the sheet:
  //   contents of rom_1 (hex, n*v repeats v):
  //   0 0 0 290 12*0 283 0 0 283 12*0 4c0 0 0 4c0 12*0 202 0 0 202 44*0 988 0 0 988 11*0 13a4
endmodule

module ALUDecoder (
  input  [1:0] ALUOp,
  input  [31:0] instr,
  output [3:0] ALUControl
);

  ROM #(.addrWidth(6), .dataWidth(4)) rom_1 (.addr({ALUOp, instr[30], instr[14:12]}), .data(ALUControl));

  // Notes on the sheet:
  //   contents of rom_1 (hex, n*v repeats v):
  //   16*2 16*a 2 5 8 9 4 6 1 0 3 5 8 9 4 7 1 0 2 5 8 9 4 6 1 0 2 5 8 9 4 7 1
endmodule

module BranchUnit (
  input  [31:0] A,
  input  in_2,
  input  [31:0] B,
  input  [2:0] funct3,
  input  Branch,
  input  Jump,
  output Taken
);

  wire and_1_out, comparator_1_eq, comparator_1_lt, comparator_2_lt, multiplexer_1_out, not_1_out, not_2_out,
       not_3_out;

  Comparator #(.width(32)) comparator_1 (.a(A), .b(B), .eq(comparator_1_eq), .lt(comparator_1_lt));  // open: gt
  Comparator #(.mode("unsigned"), .width(32)) comparator_2 (.a(A), .b(B), .lt(comparator_2_lt));  // open: gt, eq
  not not_1 (not_1_out, comparator_1_eq);
  Multiplexer #(.select(3)) multiplexer_1 (
    .in0(comparator_1_eq), .in1(not_1_out), .in2(in_2), .in3(in_2), .in4(comparator_1_lt), .in5(not_2_out),
    .in6(comparator_2_lt), .in7(not_3_out), .out(multiplexer_1_out), .sel(funct3));
  not not_2 (not_2_out, comparator_1_lt);
  not not_3 (not_3_out, comparator_2_lt);
  and and_1 (and_1_out, multiplexer_1_out, Branch);
  or or_1 (Taken, and_1_out, Jump);
endmodule

module PCUnit (
  input  clk,
  input  reset,
  input  PCEn,
  input  IsComp,
  input  [31:0] Target,
  input  Taken,
  output [31:0] PC,
  output [31:0] PCPlus
);

  wire [31:0] multiplexer_1_out, multiplexer_2_out;

  Register #(.width(32)) register_1 (.D(multiplexer_2_out), .en(PCEn), .clk(clk), .Q(PC), .clr(reset));
  Multiplexer #(.width(32)) multiplexer_1 (.in0(32'h4), .in1(32'h2), .out(multiplexer_1_out), .sel(IsComp));
  Adder #(.width(32)) adder_1 (.a(PC), .b(multiplexer_1_out), .out(PCPlus));  // open: cin, cout
  Multiplexer #(.width(32)) multiplexer_2 (.in0(PCPlus), .in1(Target), .out(multiplexer_2_out), .sel(Taken));
endmodule

module PipeReg32 (
  input  clk,
  input  reset,
  input  en,
  input  clr,
  input  [31:0] d,
  input  [31:0] in_6,
  output [31:0] q
);

  wire or_1_out;
  wire [31:0] multiplexer_1_out;

  Register #(.width(32)) register_1 (.D(multiplexer_1_out), .en(or_1_out), .clk(clk), .Q(q), .clr(reset));
  Multiplexer #(.width(32)) multiplexer_1 (.in0(d), .in1(in_6), .out(multiplexer_1_out), .sel(clr));
  or or_1 (or_1_out, en, clr);
endmodule
